// Logisim project ai + keyboard.circ as structural Verilog: 6 circuits, main circuit main
module main (
  input  in_1
);

  wire cdm_8_mark5_1_p1, cdm_8_mark5_1_p2, cdm_8_mark5_1_p4, cdm_8_mark5_1_p5, cdm_8_mark5_1_p6,
       cdm_8_mark5_1_p7, cdm_8_mark5_1_p8, cdm_8_mark5_1_p9, cdm_8_mark5_1_p13, clock, not_1_out;
  wire [7:0] cdm_8_mark5_1_p10, cdm_8_mark5_1_p11, cdm_8_mark5_1_p12, controlled_buffer_2_out, undriven;

  // Probe on cdm_8_mark5_1_p1
  Clock clock_1 (.out(clock));
  // Probe on cdm_8_mark5_1_p2
  // Probe on cdm_8_mark5_1_p4
  // Probe on cdm_8_mark5_1_p6
  // Probe on cdm_8_mark5_1_p5
  // Probe on cdm_8_mark5_1_p8
  // Probe on cdm_8_mark5_1_p7
  // CdM_8_mark5 cdm_8_mark5_1: pin names not known; wires that end beside it: cdm_8_mark5_1_p1, cdm_8_mark5_1_p2, clock, cdm_8_mark5_1_p4, cdm_8_mark5_1_p5, cdm_8_mark5_1_p6, cdm_8_mark5_1_p7, cdm_8_mark5_1_p8, cdm_8_mark5_1_p9, cdm_8_mark5_1_p10, cdm_8_mark5_1_p11, cdm_8_mark5_1_p12, cdm_8_mark5_1_p13, cdm_8_mark5_1_p10
  not not_1 (not_1_out, cdm_8_mark5_1_p9);
  assign cdm_8_mark5_1_p12 = cdm_8_mark5_1_p9 ? undriven : 8'bz;  // Controlled_Buffer controlled_buffer_1
  // Probe on cdm_8_mark5_1_p10
  assign controlled_buffer_2_out = not_1_out ? cdm_8_mark5_1_p11 : 8'bz;  // Controlled_Buffer controlled_buffer_2
  RAM ram_1 (.addr(cdm_8_mark5_1_p10), .data(controlled_buffer_2_out), .sel(cdm_8_mark5_1_p13));  // open: clk, ld, clr
  RAM #(.bus("separate")) ram_2 (
    .din(undriven), .data(controlled_buffer_2_out), .clk(clock), .ld(cdm_8_mark5_1_p9), .clr(in_1));  // open: addr, str, sel
endmodule

module keyboard (
  input  [6:0] in_1,
  output [1:0] out_2
);

  wire comparator_1_eq, comparator_2_eq, comparator_3_eq, comparator_4_eq;

  Comparator #(.width(7)) comparator_1 (.a(in_1), .b(7'b1110011), .eq(comparator_1_eq));  // open: gt, lt
  Comparator #(.width(7)) comparator_2 (.a(in_1), .b(7'b1001011), .eq(comparator_2_eq));  // open: gt, lt
  Comparator #(.width(7)) comparator_3 (.a(in_1), .b(7'b1110111), .eq(comparator_3_eq));  // open: gt, lt
  Comparator #(.width(7)) comparator_4 (.a(in_1), .b(7'b1000110), .eq(comparator_4_eq));  // open: gt, lt
  Transistor #(.\type ("n")) transistor_1 (.in(1'b1), .out(out_2[0]), .gate(comparator_1_eq));
  Pull_Resistor pull_resistor_1 (.node(out_2[0]));
  Transistor #(.\type ("n"), .gate("br")) transistor_2 (.in(1'b1), .out(out_2[0]), .gate(comparator_2_eq));
  Transistor #(.\type ("n")) transistor_3 (.in(1'b1), .out(out_2[1]), .gate(comparator_3_eq));
  Pull_Resistor pull_resistor_2 (.node(out_2[1]));
  Transistor #(.\type ("n"), .gate("br")) transistor_4 (.in(1'b1), .out(out_2[1]), .gate(comparator_4_eq));
  // Probe on out_2
endmodule

module keyboardR (
  input  [6:0] in_1,
  output [1:0] out_2
);

  wire comparator_1_eq, comparator_2_eq, comparator_3_eq, comparator_4_eq;

  Comparator #(.width(7)) comparator_1 (.a(in_1), .b(7'b1101100), .eq(comparator_1_eq));  // open: gt, lt
  Comparator #(.width(7)) comparator_2 (.a(in_1), .b(7'b0110100), .eq(comparator_2_eq));  // open: gt, lt
  Comparator #(.width(7)) comparator_3 (.a(in_1), .b(7'b1101111), .eq(comparator_3_eq));  // open: gt, lt
  Comparator #(.width(7)) comparator_4 (.a(in_1), .b(7'b1001001), .eq(comparator_4_eq));  // open: gt, lt
  Transistor #(.\type ("n")) transistor_1 (.in(1'b1), .out(out_2[0]), .gate(comparator_1_eq));
  Pull_Resistor pull_resistor_1 (.node(out_2[0]));
  Transistor #(.\type ("n"), .gate("br")) transistor_2 (.in(1'b1), .out(out_2[0]), .gate(comparator_2_eq));
  Transistor #(.\type ("n")) transistor_3 (.in(1'b1), .out(out_2[1]), .gate(comparator_3_eq));
  Pull_Resistor pull_resistor_2 (.node(out_2[1]));
  Transistor #(.\type ("n"), .gate("br")) transistor_4 (.in(1'b1), .out(out_2[1]), .gate(comparator_4_eq));
  // Probe on out_2
endmodule

module test (
);

  wire clock_1_out;
  wire [6:0] keyboard_1_data;

  Clock clock_1 (.out(clock_1_out));
  Keyboard keyboard_1 (.clk(clock_1_out), .data(keyboard_1_data));  // open: re, clr, avail
  // Probe on keyboard_1_data
endmodule

module keyboardBML (
  input  [6:0] in_1,
  output [1:0] out_2
);

  wire comparator_1_eq, comparator_2_eq, comparator_3_eq, comparator_4_eq;

  Comparator #(.width(7)) comparator_1 (.a(in_1), .b(7'b1100101), .eq(comparator_1_eq));  // open: gt, lt
  Comparator #(.width(7)) comparator_2 (.a(in_1), .b(7'b1000011), .eq(comparator_2_eq));  // open: gt, lt
  Comparator #(.width(7)) comparator_3 (.a(in_1), .b(7'b0110010), .eq(comparator_3_eq));  // open: gt, lt
  Comparator #(.width(7)) comparator_4 (.a(in_1), .b(7'b1100100), .eq(comparator_4_eq));  // open: gt, lt
  Transistor #(.\type ("n")) transistor_1 (.in(1'b1), .out(out_2[0]), .gate(comparator_1_eq));
  Pull_Resistor pull_resistor_1 (.node(out_2[0]));
  Transistor #(.\type ("n"), .gate("br")) transistor_2 (.in(1'b1), .out(out_2[0]), .gate(comparator_2_eq));
  Transistor #(.\type ("n")) transistor_3 (.in(1'b1), .out(out_2[1]), .gate(comparator_3_eq));
  Pull_Resistor pull_resistor_2 (.node(out_2[1]));
  Transistor #(.\type ("n"), .gate("br")) transistor_4 (.in(1'b1), .out(out_2[1]), .gate(comparator_4_eq));
  // Probe on out_2
endmodule

module keyboardBMR (
  input  [6:0] in_1,
  output [1:0] out_2
);

  wire comparator_1_eq, comparator_2_eq, comparator_3_eq, comparator_4_eq;

  Comparator #(.width(7)) comparator_1 (.a(in_1), .b(7'b1110000), .eq(comparator_1_eq));  // open: gt, lt
  Comparator #(.width(7)) comparator_2 (.a(in_1), .b(7'b0110111), .eq(comparator_2_eq));  // open: gt, lt
  Comparator #(.width(7)) comparator_3 (.a(in_1), .b(7'b0110110), .eq(comparator_3_eq));  // open: gt, lt
  Comparator #(.width(7)) comparator_4 (.a(in_1), .b(7'b0111011), .eq(comparator_4_eq));  // open: gt, lt
  Transistor #(.\type ("n")) transistor_1 (.in(1'b1), .out(out_2[0]), .gate(comparator_1_eq));
  Pull_Resistor pull_resistor_1 (.node(out_2[0]));
  Transistor #(.\type ("n"), .gate("br")) transistor_2 (.in(1'b1), .out(out_2[0]), .gate(comparator_2_eq));
  Transistor #(.\type ("n")) transistor_3 (.in(1'b1), .out(out_2[1]), .gate(comparator_3_eq));
  Pull_Resistor pull_resistor_2 (.node(out_2[1]));
  Transistor #(.\type ("n"), .gate("br")) transistor_4 (.in(1'b1), .out(out_2[1]), .gate(comparator_4_eq));
  // Probe on out_2
endmodule
