// Logisim project ai.circ as structural Verilog: 1 circuit, main circuit main
module main (
  input  in_1
);

  wire cdm_8_mark5_1_p2, cdm_8_mark5_1_p3, cdm_8_mark5_1_p4, cdm_8_mark5_1_p5, cdm_8_mark5_1_p9, clock,
       not_1_out;
  wire [7:0] cdm_8_mark5_1_p6, cdm_8_mark5_1_p7, cdm_8_mark5_1_p8, controlled_buffer_2_out, undriven;

  Clock clock_1 (.out(clock));
  // Probe on cdm_8_mark5_1_p2
  // Probe on cdm_8_mark5_1_p3
  // Probe on cdm_8_mark5_1_p4
  // CdM_8_mark5 cdm_8_mark5_1: pin names not known; wires that end beside it: clock, cdm_8_mark5_1_p2, cdm_8_mark5_1_p3, cdm_8_mark5_1_p4, cdm_8_mark5_1_p5, cdm_8_mark5_1_p6, cdm_8_mark5_1_p7, cdm_8_mark5_1_p8, cdm_8_mark5_1_p9, cdm_8_mark5_1_p6
  not not_1 (not_1_out, cdm_8_mark5_1_p5);
  assign cdm_8_mark5_1_p8 = cdm_8_mark5_1_p5 ? undriven : 8'bz;  // Controlled_Buffer controlled_buffer_1
  // Probe on cdm_8_mark5_1_p6
  assign controlled_buffer_2_out = not_1_out ? cdm_8_mark5_1_p7 : 8'bz;  // Controlled_Buffer controlled_buffer_2
  RAM ram_1 (.addr(cdm_8_mark5_1_p6), .data(controlled_buffer_2_out), .sel(cdm_8_mark5_1_p9));  // open: clk, ld, clr
  RAM #(.bus("separate")) ram_2 (
    .din(undriven), .data(controlled_buffer_2_out), .clk(clock), .ld(cdm_8_mark5_1_p5), .clr(in_1));  // open: addr, str, sel
endmodule
