// Logisim project tennis.circ as structural Verilog: 8 circuits, main circuit main
module main (
  input  AI,
  input  Stupidness
);

  wire button_1_out, clock;
  wire [2:0] controller_1_out_8;
  wire [4:0] controller_1_ballx, controller_1_bally, controller_1_out_9, controller_1_out_11,
       controller_1_out_12, display_1_out_14, display_1_out_15, display_1_out_16, display_1_out_17,
       display_1_out_18, display_2_out_14, display_2_out_15, display_2_out_16, display_2_out_17,
       display_2_out_18, display_3_out_14, display_3_out_15, display_3_out_16, display_3_out_17,
       display_3_out_18;
  wire [6:0] keyboard_1_data;
  wire [7:0] player1, player2;
  wire [31:0] display_1_out_6, display_1_out_7, display_1_out_8, display_1_out_9, display_1_out_10,
       display_1_out_11, display_1_out_12, display_1_out_13, display_2_out_6, display_2_out_7,
       display_2_out_8, display_2_out_9, display_2_out_10, display_2_out_11, display_2_out_12,
       display_2_out_13, display_3_out_6, display_3_out_7, display_3_out_8, display_3_out_9,
       display_3_out_10, display_3_out_11, display_3_out_12, display_3_out_13, display_4_out_6,
       display_4_out_7, display_4_out_8, display_4_out_9, display_4_out_10, display_4_out_11,
       display_4_out_12, display_4_out_13;

  Clock clock_1 (.out(clock));
  Keyboard keyboard_1 (.clk(clock), .data(keyboard_1_data));  // open: re, clr, avail
  Button button_1 (.out(button_1_out));
  Hex_Digit_Display hex_digit_display_1 (.value(player1[7:4]));  // open: dp
  Hex_Digit_Display hex_digit_display_2 (.value(player1[3:0]));  // open: dp
  DotMatrix #(.matrixcols(32), .matrixrows(32)) dotmatrix_1 (
    .col0(display_1_out_6), .col1(display_1_out_7), .col2(display_1_out_8), .col3(display_1_out_9),
    .col4(display_1_out_10), .col5(display_1_out_11), .col6(display_1_out_12), .col7(display_1_out_13),
    .col8(display_2_out_6), .col9(display_2_out_7), .col10(display_2_out_8), .col11(display_2_out_9),
    .col12(display_2_out_10), .col13(display_2_out_11), .col14(display_2_out_12), .col15(display_2_out_13),
    .col16(display_3_out_6), .col17(display_3_out_7), .col18(display_3_out_8), .col19(display_3_out_9),
    .col20(display_3_out_10), .col21(display_3_out_11), .col22(display_3_out_12), .col23(display_3_out_13),
    .col24(display_4_out_6), .col25(display_4_out_7), .col26(display_4_out_8), .col27(display_4_out_9),
    .col28(display_4_out_10), .col29(display_4_out_11), .col30(display_4_out_12), .col31(display_4_out_13));
  controller controller_1 (
    .in_1(button_1_out), .keyboard_in(keyboard_1_data), .out_9(controller_1_out_9),
    .ballX(controller_1_ballx), .ballY(controller_1_bally), .out_11(controller_1_out_11),
    .out_12(controller_1_out_12), .out_5(player1), .out_6(player2), .in_2(AI), .out_8(controller_1_out_8),
    .in_3(Stupidness));
  // Probe on controller_1_out_8
  display display_1 (
    .in_1(controller_1_out_9), .in_2(controller_1_ballx), .in_3(controller_1_bally),
    .in_4(controller_1_out_11), .in_5(controller_1_out_12), .out_14(display_1_out_14),
    .out_15(display_1_out_15), .out_16(display_1_out_16), .out_17(display_1_out_17),
    .out_18(display_1_out_18), .out_8(display_1_out_8), .out_6(display_1_out_6), .out_7(display_1_out_7),
    .out_9(display_1_out_9), .out_10(display_1_out_10), .out_11(display_1_out_11), .out_12(display_1_out_12),
    .out_13(display_1_out_13));
  display display_2 (
    .in_1(display_1_out_14), .in_2(display_1_out_15), .in_3(display_1_out_16), .in_4(display_1_out_17),
    .in_5(display_1_out_18), .out_14(display_2_out_14), .out_15(display_2_out_15), .out_16(display_2_out_16),
    .out_17(display_2_out_17), .out_18(display_2_out_18), .out_8(display_2_out_8), .out_6(display_2_out_6),
    .out_7(display_2_out_7), .out_9(display_2_out_9), .out_10(display_2_out_10), .out_11(display_2_out_11),
    .out_12(display_2_out_12), .out_13(display_2_out_13));
  display display_3 (
    .in_1(display_2_out_14), .in_2(display_2_out_15), .in_3(display_2_out_16), .in_4(display_2_out_17),
    .in_5(display_2_out_18), .out_14(display_3_out_14), .out_15(display_3_out_15), .out_16(display_3_out_16),
    .out_17(display_3_out_17), .out_18(display_3_out_18), .out_8(display_3_out_8), .out_6(display_3_out_6),
    .out_7(display_3_out_7), .out_9(display_3_out_9), .out_10(display_3_out_10), .out_11(display_3_out_11),
    .out_12(display_3_out_12), .out_13(display_3_out_13));
  display display_4 (
    .in_1(display_3_out_14), .in_2(display_3_out_15), .in_3(display_3_out_16), .in_4(display_3_out_17),
    .in_5(display_3_out_18), .out_8(display_4_out_8), .out_6(display_4_out_6), .out_7(display_4_out_7),
    .out_9(display_4_out_9), .out_10(display_4_out_10), .out_11(display_4_out_11), .out_12(display_4_out_12),
    .out_13(display_4_out_13));  // open: out_14, out_15, out_16, out_17, out_18
  Hex_Digit_Display hex_digit_display_3 (.value(player2[3:0]));  // open: dp
  Hex_Digit_Display hex_digit_display_4 (.value(player2[7:4]));  // open: dp

  // Notes on the sheet:
  //   START
  //   0 - genious
  //   1 - stupid
endmodule

module inc (
  input  [4:0] in_1,
  output [4:0] out_2
);

  Adder #(.width(5)) adder_1 (.a(in_1), .b(5'b00001), .out(out_2));  // open: cin, cout
endmodule

module display (
  input  [4:0] in_1,
  input  [4:0] in_2,
  input  [4:0] in_3,
  input  [4:0] in_4,
  input  [4:0] in_5,
  output [31:0] out_6,
  output [31:0] out_7,
  output [31:0] out_8,
  output [31:0] out_9,
  output [31:0] out_10,
  output [31:0] out_11,
  output [31:0] out_12,
  output [31:0] out_13,
  output [4:0] out_14,
  output [4:0] out_15,
  output [4:0] out_16,
  output [4:0] out_17,
  output [4:0] out_18
);

  wire _0, _1, _2, _3, _4, _5, _6, _7, comparator_1_eq, comparator_2_eq, comparator_3_eq;
  wire [4:0] divider_1_out, divider_1_rem;
  wire [31:0] l_bat32, multiplexer_1_out, multiplexer_2_out, multiplexer_3_out, multiplexer_4_out,
       multiplexer_5_out, multiplexer_6_out, multiplexer_7_out, multiplexer_8_out, pull_resistor_4_node,
       pull_resistor_7_node, r_bat32, y32;

  assign out_6 = {32{1'b0}} | multiplexer_1_out;  // OR_Gate or_1, 32 bits wide
  Multiplexer #(.width(32)) multiplexer_1 (.in0({32{1'b0}}), .in1(y32), .out(multiplexer_1_out), .sel(_0));  // open: en
  Pull_Resistor pull_resistor_1 (.node(_0));
  Pull_Resistor pull_resistor_2 (.node(_1));
  assign out_7 = {32{1'b0}} | multiplexer_2_out;  // OR_Gate or_2, 32 bits wide
  Multiplexer #(.width(32)) multiplexer_2 (.in0({32{1'b0}}), .in1(y32), .out(multiplexer_2_out), .sel(_1));  // open: en
  Comparator #(.width(5), .mode("unsigned")) comparator_1 (
    .a(in_1), .b({5{1'b0}}), .eq(comparator_1_eq));  // open: gt, lt
  assign out_8 = {32{1'b0}} | multiplexer_3_out;  // OR_Gate or_3, 32 bits wide
  Multiplexer #(.width(32)) multiplexer_3 (.in0({32{1'b0}}), .in1(y32), .out(multiplexer_3_out), .sel(_2));  // open: en
  Pull_Resistor pull_resistor_3 (.node(_2));
  Pull_Resistor pull_resistor_4 (.node(pull_resistor_4_node));
  assign pull_resistor_4_node = comparator_1_eq ? l_bat32 : 32'bz;  // Controlled_Buffer controlled_buffer_1
  assign out_9 = {32{1'b0}} | pull_resistor_4_node | multiplexer_4_out;  // OR_Gate or_4, 32 bits wide
  Multiplexer #(.width(32)) multiplexer_4 (.in0({32{1'b0}}), .in1(y32), .out(multiplexer_4_out), .sel(_3));  // open: en
  Pull_Resistor pull_resistor_5 (.node(_3));
  Comparator #(.width(5), .mode("unsigned")) comparator_2 (
    .a(in_1), .b(5'b00011), .eq(comparator_2_eq));  // open: gt, lt
  inc inc_1 (.in_1(in_1), .out_2(out_14));
  assign out_10 = {32{1'b0}} | pull_resistor_7_node | multiplexer_5_out;  // OR_Gate or_5, 32 bits wide
  Pull_Resistor pull_resistor_6 (.node(_4));
  Pull_Resistor pull_resistor_7 (.node(pull_resistor_7_node));
  assign pull_resistor_7_node = comparator_2_eq ? r_bat32 : 32'bz;  // Controlled_Buffer controlled_buffer_2
  Multiplexer #(.width(32)) multiplexer_5 (.in0({32{1'b0}}), .in1(y32), .out(multiplexer_5_out), .sel(_4));  // open: en
  assign out_11 = {32{1'b0}} | multiplexer_6_out;  // OR_Gate or_6, 32 bits wide
  Pull_Resistor pull_resistor_8 (.node(_5));
  Comparator #(.width(5)) comparator_3 (.a(in_1), .b(divider_1_out), .eq(comparator_3_eq));  // open: gt, lt
  Divider #(.width(5)) divider_1 (.a(in_2), .b(5'b01000), .out(divider_1_out), .rem(divider_1_rem));  // open: upper
  Multiplexer #(.width(32)) multiplexer_6 (.in0({32{1'b0}}), .in1(y32), .out(multiplexer_6_out), .sel(_5));  // open: en
  Shifter #(.width(32)) shifter_1 (.in(32'h1), .\dist (in_3), .out(y32));
  Shifter #(.width(32)) shifter_2 (.in(32'h7), .\dist (in_4), .out(l_bat32));
  Shifter #(.width(32)) shifter_3 (.in(32'h7), .\dist (in_5), .out(r_bat32));
  assign out_12 = {32{1'b0}} | multiplexer_7_out;  // OR_Gate or_7, 32 bits wide
  Pull_Resistor pull_resistor_9 (.node(_6));
  Decoder #(.select(3)) decoder_1 (
    .out0(_0), .out1(_1), .out2(_2), .out3(_3), .out4(_4), .out5(_5), .out6(_6), .out7(_7),
    .sel(divider_1_rem[2:0]), .en(comparator_3_eq));
  Multiplexer #(.width(32)) multiplexer_7 (.in0({32{1'b0}}), .in1(y32), .out(multiplexer_7_out), .sel(_6));  // open: en
  assign out_13 = {32{1'b0}} | multiplexer_8_out;  // OR_Gate or_8, 32 bits wide
  Multiplexer #(.width(32)) multiplexer_8 (.in0({32{1'b0}}), .in1(y32), .out(multiplexer_8_out), .sel(_7));  // open: en
  Pull_Resistor pull_resistor_10 (.node(_7));

  assign out_15 = in_2;
  assign out_16 = in_3;
  assign out_17 = in_4;
  assign out_18 = in_5;

  // Other names for the same wires on the sheet: l_bat[4:0] = in_4; r_bat[4:0] = in_5; y[4:0] = in_3
endmodule

// 2
module controller (
  input  in_1,
  input  in_2,
  input  in_3,
  input  [6:0] keyboard_in,
  output [7:0] out_5,
  output [7:0] out_6,
  output [4:0] ballX,
  output [2:0] out_8,
  output [4:0] out_9,
  output [4:0] ballY,
  output [4:0] out_11,
  output [4:0] out_12
);

  wire adder_1_cout, adder_2_cout, and_1_out, and_2_out, and_3_out, and_4_out, and_5_out, and_6_out,
       and_7_out, and_8_out, and_9_out, and_10_out, and_11_out, and_12_out, and_13_out, and_14_out,
       and_15_out, and_16_out, and_17_out, and_18_out, and_19_out, bot, center, check_collision_2_out_8,
       check_collision_3_out_8, clock, col, comparator_1_eq, comparator_2_eq, comparator_3_gt,
       comparator_3_lt, comparator_4_gt, comparator_4_lt, comparator_5_lt, comparator_6_eq, comparator_7_eq,
       comparator_8_eq, comparator_9_eq, comparator_10_gt, comparator_11_gt, comparator_12_eq,
       comparator_12_gt, comparator_12_lt, counter_3_carry, counter_4_carry, counter_5_carry, counter_6_q,
       counter_8_carry, counter_11_carry, d_ff_1_q, d_ff_2_q, d_ff_3_q, d_ff_4_q, multiplexer_6_out,
       multiplexer_10_out, multiplexer_11_out, multiplexer_12_out, multiplexer_15_out, not_1_out, not_2_out,
       not_3_out, not_4_out, not_5_out, not_6_out, not_7_out, not_9_out, not_10_out, not_11_out, not_12_out,
       not_13_out, not_14_out, not_15_out, not_16_out, not_17_out, not_18_out, or_1_out, or_2_out, or_3_out,
       or_4_out, or_5_out, or_6_out, or_9_out, or_10_out, p1g, p2g, switch_x, switch_y, top, undriven,
       undriven_2, xor_1_out, xor_2_out, z;
  wire [1:0] keyboard_1_out_2, keyboardr_1_out_2, random_1_out, random_2_out, random_3_out;
  wire [2:0] aiy, counter_9_q, multiplexer_2_out, multiplexer_4_out, multiplexer_5_out, multiplexer_7_out,
       multiplexer_13_out, multiplexer_14_out, negator_1_out, negator_2_out, new_vx, new_vy, undriven_3, vx,
       vy;
  wire [4:0] adder_1_out, adder_2_out, adder_5_out, bit_extender_3_out, main_1_out_8, multiplexer_8_out,
       multiplexer_9_out, random_4_out, subtractor_1_out, subtractor_2_out, subtractor_3_out;
  wire [5:0] random_5_out;
  wire [7:0] adder_3_out, adder_4_out, bit_extender_1_out, bit_extender_2_out, multiplexer_1_out,
       multiplexer_3_out, oldx, oldy, x, y;

  Clock clock_1 (.out(z));
  Multiplexer #(.width(8)) multiplexer_1 (
    .in0({ballX, multiplexer_7_out}), .in1(8'h76), .out(multiplexer_1_out), .sel(in_1));  // open: en
  Register #(.width(3)) u_vx (.D(multiplexer_2_out), .Q(out_8), .clk(clock));  // open: en, clr
  Multiplexer #(.width(3)) multiplexer_2 (.in0(new_vx), .in1(3'b010), .out(multiplexer_2_out), .sel(in_1));  // open: en
  Multiplexer #(.width(8)) multiplexer_3 (
    .in0({ballY, multiplexer_5_out}), .in1(8'h76), .out(multiplexer_3_out), .sel(in_1));  // open: en
  Register u_y (.D(multiplexer_3_out), .Q(oldy), .clk(clock));  // open: en, clr
  Register #(.width(3)) u_vy (.D(multiplexer_4_out), .Q(aiy), .clk(clock));  // open: en, clr
  Multiplexer #(.width(3)) multiplexer_4 (.in0(new_vy), .in1(3'b001), .out(multiplexer_4_out), .sel(in_1));  // open: en
  Adder #(.width(5)) adder_1 (.a(out_11), .b(5'b00011), .out(adder_1_out), .cout(adder_1_cout));  // open: cin
  Subtractor #(.width(5)) subtractor_1 (
    .a(out_11), .b(5'b00001), .out(subtractor_1_out), .bin(adder_1_cout));  // open: bout
  Comparator #(.width(5)) comparator_1 (.a(5'b00011), .b(ballX), .eq(comparator_1_eq));  // open: gt, lt
  keyboard keyboard_1 (.in_1(keyboard_in), .out_2(keyboard_1_out_2));
  keyboardR keyboardr_1 (.in_1(keyboard_in), .out_2(keyboardr_1_out_2));
  Adder #(.width(5)) adder_2 (.a(out_12), .b(5'b00011), .out(adder_2_out), .cout(adder_2_cout));  // open: cin
  Subtractor #(.width(5)) subtractor_2 (
    .a(out_12), .b(5'b00001), .out(subtractor_2_out), .bin(adder_2_cout));  // open: bout
  Comparator #(.width(5)) comparator_2 (.a(5'b11100), .b(ballX), .eq(comparator_2_eq));  // open: gt, lt
  Register u_x (.D(multiplexer_1_out), .Q(oldx), .clk(clock));  // open: en, clr
  motion motion_1 (.coord(oldy), .speed(aiy), .new_cords(y), .new_speed(vy));  // open: p1goal, p2goal
  Comparator #(.width(2)) comparator_3 (
    .a(keyboard_1_out_2), .b(2'b00), .gt(comparator_3_gt), .lt(comparator_3_lt));  // open: eq
  Comparator #(.width(2)) comparator_4 (
    .a(keyboardr_1_out_2), .b(2'b00), .gt(comparator_4_gt), .lt(comparator_4_lt));  // open: eq
  motion motion_2 (.coord(oldx), .speed(out_8), .p1goal(p1g), .p2goal(p2g), .new_cords(x), .new_speed(vx));
  Comparator #(.width(5)) comparator_5 (.a({5{1'b0}}), .b(ballX), .lt(comparator_5_lt));  // open: gt, eq
  Comparator #(.width(5)) comparator_6 (.a(adder_1_out), .b(ballY), .eq(comparator_6_eq));  // open: gt, lt
  or or_1 (or_1_out, comparator_6_eq, comparator_7_eq);
  Comparator #(.width(5)) comparator_7 (.a(subtractor_1_out), .b(ballY), .eq(comparator_7_eq));  // open: gt, lt
  and and_1 (and_1_out, comparator_3_gt, not_1_out);
  not not_1 (not_1_out, comparator_3_lt);
  not not_2 (not_2_out, comparator_3_gt);
  and and_2 (and_2_out, not_2_out, comparator_3_lt);
  and and_3 (and_3_out, comparator_3_gt, not_3_out);
  not not_3 (not_3_out, comparator_3_lt);
  and and_4 (and_4_out, comparator_4_gt, not_4_out);
  not not_4 (not_4_out, comparator_4_lt);
  not not_5 (not_5_out, comparator_4_gt);
  and and_5 (and_5_out, not_5_out, comparator_4_lt);
  and and_6 (and_6_out, comparator_4_gt, not_6_out);
  not not_6 (not_6_out, comparator_4_lt);
  Comparator #(.width(5)) comparator_8 (.a(adder_2_out), .b(ballY), .eq(comparator_8_eq));  // open: gt, lt
  or or_2 (or_2_out, comparator_8_eq, comparator_9_eq);
  Comparator #(.width(5)) comparator_9 (.a(subtractor_2_out), .b(ballY), .eq(comparator_9_eq));  // open: gt, lt
  Comparator #(.width(5)) comparator_10 (.a({5{1'b0}}), .b(ballX), .gt(comparator_10_gt));  // open: eq, lt
  or or_3 (or_3_out, switch_x, switch_y);
  check_collision check_collision_1 (
    .x(x), .y(y), .bat_left(out_11), .bat_right(out_12), .out_8(col), .top(top), .center(center), .bot(bot));
  or or_4 (or_4_out, switch_y, switch_x);
  Multiplexer #(.width(8), .enable("false")) multiplexer_5 (
    .in0(y), .in1(oldy), .out({ballY, multiplexer_5_out}), .sel(or_4_out));
  Multiplexer #(.disabled(0), .enable("false")) multiplexer_6 (
    .in0(comparator_5_lt), .out(multiplexer_6_out), .sel(in_2));  // open: in1
  and and_7 (and_7_out, or_1_out, comparator_1_eq);
  or or_5 (or_5_out, and_2_out, and_3_out);
  or or_6 (or_6_out, and_5_out, and_6_out);
  and and_8 (and_8_out, or_2_out, comparator_2_eq);
  Multiplexer #(.width(8), .enable("false")) multiplexer_7 (
    .in0(x), .in1(oldx), .out({ballX, multiplexer_7_out}), .sel(or_3_out));
  and and_9 (and_9_out, multiplexer_6_out, ~and_7_out, or_5_out);  // AND_Gate
  and and_10 (and_10_out, or_6_out, ~and_8_out, comparator_10_gt);  // AND_Gate
  Negator #(.width(3)) negator_1 (.in(vx), .out(negator_1_out));
  Negator #(.width(3)) negator_2 (.in(vy), .out(negator_2_out));
  Counter #(.width(5), .max('h1d), .ongoal("stay")) counter_1 (
    .load(and_1_out), .D(out_11), .count(and_9_out), .Q(out_11), .clk(z));  // open: carry, clr
  ai___keyboard_main main_1 (
    .vx(out_8), .x(oldx), .y(oldy), .vy(aiy), .bat_l(out_11), .out_8(main_1_out_8));  // open: start, rg
  Random #(.width(2), .seed(5)) random_1 (.clk(z), .out(random_1_out));  // open: next, clr
  Random #(.width(2), .seed(12315)) random_2 (.clk(counter_5_carry), .out(random_2_out));  // open: next, clr
  assign bit_extender_1_out = {{5{negator_1_out[2]}}, negator_1_out};  // Bit_Extender bit_extender_1
  assign bit_extender_2_out = {{5{negator_2_out[2]}}, negator_2_out};  // Bit_Extender bit_extender_2
  assign bit_extender_3_out = {{3{1'b0}}, random_1_out};  // Bit_Extender bit_extender_3
  Comparator #(.width(2), .mode("unsigned")) comparator_11 (
    .a(random_2_out), .b(2'b01), .gt(comparator_11_gt));  // open: eq, lt
  Adder adder_3 (.a(x), .b(bit_extender_1_out), .out(adder_3_out));  // open: cin, cout
  Adder adder_4 (.a(y), .b(bit_extender_2_out), .out(adder_4_out));  // open: cin, cout
  not not_7 (not_7_out, d_ff_1_q);
  D_Flip_Flop d_ff_1 (.clk(z), .D(not_7_out), .Q(d_ff_1_q));  // open: Qn, preset, en, reset
  Subtractor #(.width(5)) subtractor_3 (
    .a(main_1_out_8), .b(bit_extender_3_out), .out(subtractor_3_out));  // open: bin, bout
  Adder #(.width(5)) adder_5 (.a(main_1_out_8), .b(bit_extender_3_out), .out(adder_5_out));  // open: cin, cout
  check_collision check_collision_2 (
    .x(adder_3_out), .y(y), .bat_left(out_11), .bat_right(out_12), .out_8(check_collision_2_out_8));  // open: top, center, bot
  check_collision check_collision_3 (
    .x(x), .y(adder_4_out), .bat_left(out_11), .bat_right(out_12), .out_8(check_collision_3_out_8));  // open: top, center, bot
  D_Flip_Flop d_ff_2 (.clk(not_7_out), .D(clock), .Q(d_ff_2_q));  // open: Qn, preset, en, reset
  not not_8 (clock, d_ff_2_q);
  Multiplexer #(.width(5), .disabled(0), .enable("false")) multiplexer_8 (
    .in0(subtractor_3_out), .in1(adder_5_out), .out(multiplexer_8_out), .sel(comparator_11_gt));
  Multiplexer #(.width(5), .disabled(0), .enable("false")) multiplexer_9 (
    .in0(multiplexer_8_out), .in1(main_1_out_8), .out(multiplexer_9_out), .sel(comparator_11_gt));
  and and_11 (and_11_out, ~check_collision_2_out_8, col);  // AND_Gate
  and and_12 (and_12_out, check_collision_2_out_8, col, check_collision_3_out_8);
  and and_13 (and_13_out, ~check_collision_3_out_8, col);  // AND_Gate
  D_Flip_Flop d_ff_3 (.clk(clock), .D(not_9_out), .Q(d_ff_3_q));  // open: Qn, preset, en, reset
  not not_9 (not_9_out, d_ff_3_q);
  Comparator #(.width(5), .mode("unsigned")) comparator_12 (
    .a(multiplexer_9_out), .b(out_12), .gt(comparator_12_gt), .eq(comparator_12_eq), .lt(comparator_12_lt));
  Random #(.width(2), .seed(12315)) random_3 (.out(random_3_out));  // open: clk, next, clr
  Comparator #(.width(2), .mode("unsigned")) comparator_13 (.a(random_3_out), .b(2'b01));  // open: gt, eq, lt
  or or_7 (switch_x, and_11_out, and_12_out);
  or or_8 (switch_y, and_12_out, and_13_out);
  D_Flip_Flop d_ff_4 (.clk(not_9_out), .D(not_10_out), .Q(d_ff_4_q));  // open: Qn, preset, en, reset
  not not_10 (not_10_out, d_ff_4_q);
  Multiplexer #(.disabled(0), .enable("false")) multiplexer_10 (
    .in0(and_4_out), .in1(comparator_12_lt), .out(multiplexer_10_out), .sel(in_2));
  Multiplexer #(.disabled(0), .enable("false")) multiplexer_11 (
    .in0(and_10_out), .in1(not_11_out), .out(multiplexer_11_out), .sel(in_2));
  not not_11 (not_11_out, comparator_12_eq);
  update_vy update_vy_1 (.old_vy(vy), .\output (new_vy), .top(top), .center(center), .bot(bot), .ds(1'b0));
  D_Flip_Flop d_ff_5 (.clk(not_10_out));  // open: D, Q, Qn, preset, en, reset
  xor xor_1 (xor_1_out, vx[2], switch_x);
  Counter #(.width(5), .max('h1d), .ongoal("stay")) counter_2 (
    .load(multiplexer_10_out), .D(out_12), .count(multiplexer_11_out), .Q(out_12), .clk(multiplexer_12_out));  // open: carry, clr
  Multiplexer #(.disabled(0), .enable("false")) multiplexer_12 (
    .in0(z), .in1(multiplexer_15_out), .out(multiplexer_12_out), .sel(in_2));
  Counter #(.width(4), .max('hf), .ongoal("load")) counter_3 (
    .count(z), .carry(counter_3_carry), .clk(z));  // open: load, D, Q, clr
  Random #(.width(5)) random_4 (.clk(z), .out(random_4_out));  // open: next, clr
  Counter #(.width(5), .max('h1f), .ongoal("load")) counter_4 (
    .D(random_4_out), .count(z), .carry(counter_4_carry), .clk(z));  // open: load, Q, clr
  Random #(.width(6)) random_5 (.clk(z), .out(random_5_out));  // open: next, clr
  Counter #(.width(6), .max('h3f), .ongoal("load")) counter_5 (
    .D(random_5_out), .count(z), .carry(counter_5_carry), .clk(z));  // open: load, Q, clr
  Multiplexer #(.width(3), .disabled(0), .enable("false")) multiplexer_13 (
    .in0(3'b011), .in1(3'b101), .out(multiplexer_13_out), .sel(xor_2_out));
  xor xor_2 (xor_2_out, vx[2], switch_x);
  Multiplexer #(.width(3), .enable("false")) multiplexer_14 (
    .in0(3'b010), .in1(3'b110), .out(multiplexer_14_out), .sel(xor_1_out));
  Counter #(.width(1), .max('h1), .ongoal("stay")) counter_6 (
    .Q(counter_6_q), .clk(and_14_out), .clr(or_9_out));  // open: load, D, count, carry
  and and_14 (and_14_out, center, ~or_9_out);  // AND_Gate
  or or_9 (or_9_out, top, bot);
  Multiplexer #(.disabled(0), .enable("false")) multiplexer_15 (
    .in0(counter_3_carry), .in1(counter_4_carry), .out(multiplexer_15_out), .sel(in_3));
  Multiplexer #(.width(3), .enable("false")) multiplexer_16 (
    .in0(multiplexer_13_out), .in1(multiplexer_14_out), .out(new_vx), .sel(not_12_out));
  not not_12 (not_12_out, counter_6_q);
  not not_13 (not_13_out, undriven_2);
  not not_14 (not_14_out, undriven);
  not not_15 (not_15_out, undriven_2);
  and and_15 (and_15_out, undriven, not_13_out);
  and and_16 (and_16_out, not_14_out, undriven_2);
  or or_10 (or_10_out, and_16_out, and_17_out);
  and and_17 (and_17_out, undriven, not_15_out);
  Counter #(.width(4), .max('h9), .trigger("falling")) counter_7 (
    .Q(out_5[7:4]), .clk(counter_8_carry), .clr(in_1));  // open: load, D, count, carry
  Counter #(.width(4), .max('h9)) counter_8 (
    .Q(out_5[3:0]), .carry(counter_8_carry), .clk(and_18_out), .clr(in_1));  // open: load, D, count
  and and_18 (and_18_out, not_16_out, p1g);
  not not_16 (not_16_out, col);
  Counter #(.width(3), .max('h7), .ongoal("stay")) counter_9 (
    .load(and_15_out), .D(undriven_3), .count(or_10_out), .Q(counter_9_q), .clk(clock));  // open: carry, clr
  Controlled_Buffer #(.width(3)) controlled_buffer_1 (.in(counter_9_q), .en(or_10_out));  // open: out
  Counter #(.width(4), .max('h9), .trigger("falling")) counter_10 (
    .Q(out_6[7:4]), .clk(counter_11_carry), .clr(in_1));  // open: load, D, count, carry
  Counter #(.width(4), .max('h9)) counter_11 (
    .Q(out_6[3:0]), .carry(counter_11_carry), .clk(and_19_out), .clr(in_1));  // open: load, D, count
  and and_19 (and_19_out, not_17_out, not_18_out, p2g);
  not not_17 (not_17_out, p1g);
  not not_18 (not_18_out, col);

  assign out_9 = {5{1'b0}};

  // Other names for the same wires on the sheet: AI = in_2; aix[2:0] = out_8; bat1[4:0] = out_11; bat2[4:0] = out_12;
  //   Keyboard[6:0] = keyboard_in; reg = clock; reset = in_1; Stupidness = in_3
endmodule

module reflect (
  input  [2:0] speed,
  input  cout,
  output [2:0] out_3,
  output out_4,
  output p2goal,
  output p1goal
);

  wire and_2_out, not_1_out;
  wire [2:0] negator_1_out;

  Negator #(.width(3)) negator_1 (.in(speed), .out(negator_1_out));
  xor xor_1 (out_4, speed[2], cout);
  Multiplexer #(.width(3)) multiplexer_1 (.in0(speed), .in1(negator_1_out), .out(out_3), .sel(out_4));  // open: en
  and and_1 (p2goal, out_4, speed[2]);
  and and_2 (and_2_out, out_4, cout);
  not not_1 (not_1_out, p2goal);
  and and_3 (p1goal, not_1_out, and_2_out);
endmodule

module motion (
  input  [7:0] coord,
  input  [2:0] speed,
  output [7:0] new_cords,
  output [2:0] new_speed,
  output p1goal,
  output p2goal
);

  wire adder_1_cout, reflect_1_out_4;
  wire [7:0] adder_1_out, adder_2_out, bit_extender_1_out, bit_extender_2_out;

  assign bit_extender_1_out = {{5{speed[2]}}, speed};  // Bit_Extender bit_extender_1
  Adder adder_1 (.a(coord), .b(bit_extender_1_out), .out(adder_1_out), .cout(adder_1_cout));  // open: cin
  assign bit_extender_2_out = {{5{new_speed[2]}}, new_speed};  // Bit_Extender bit_extender_2
  reflect reflect_1 (
    .speed(speed), .cout(adder_1_cout), .out_3(new_speed), .out_4(reflect_1_out_4), .p2goal(p2goal),
    .p1goal(p1goal));
  Adder adder_2 (.a(coord), .b(bit_extender_2_out), .out(adder_2_out));  // open: cin, cout
  Multiplexer #(.width(8), .enable("false")) multiplexer_1 (
    .in0(adder_1_out), .in1(adder_2_out), .out(new_cords), .sel(reflect_1_out_4));
endmodule

module check_collision (
  input  [7:0] x,
  input  [7:0] y,
  input  [4:0] bat_left,
  input  [4:0] bat_right,
  output top,
  output center,
  output bot,
  output out_8
);

  wire and_1_out, and_2_out, and_3_out, and_4_out, and_5_out, and_6_out, and_7_out, and_8_out, bl, br, cl,
       cr, lc, or_1_out, or_2_out, rc, tl, tr;
  wire [4:0] inc_1_out_2, inc_2_out_2, inc_3_out_2, inc_4_out_2;

  inc inc_1 (.in_1(bat_right), .out_2(inc_1_out_2));
  inc inc_2 (.in_1(bat_left), .out_2(inc_2_out_2));
  inc inc_3 (.in_1(inc_2_out_2), .out_2(inc_3_out_2));
  inc inc_4 (.in_1(inc_1_out_2), .out_2(inc_4_out_2));
  Comparator #(.width(5)) comparator_1 (.a(y[7:3]), .b(bat_left), .eq(bl));  // open: gt, lt
  Comparator #(.width(5)) comparator_2 (.a(y[7:3]), .b(inc_2_out_2), .eq(cl));  // open: gt, lt
  Comparator #(.width(5)) comparator_3 (.a(y[7:3]), .b(inc_3_out_2), .eq(tl));  // open: gt, lt
  Comparator #(.width(5), .mode("unsigned")) comparator_4 (.a(x[7:3]), .b(5'b11100), .eq(rc));  // open: gt, lt
  Comparator #(.width(5)) comparator_5 (.a(y[7:3]), .b(bat_right), .eq(br));  // open: gt, lt
  Comparator #(.width(5)) comparator_6 (.a(y[7:3]), .b(inc_1_out_2), .eq(cr));  // open: gt, lt
  Comparator #(.width(5)) comparator_7 (.a(y[7:3]), .b(inc_4_out_2), .eq(tr));  // open: gt, lt
  Comparator #(.width(5), .mode("unsigned")) comparator_8 (.a(x[7:3]), .b(5'b00011), .eq(lc));  // open: gt, lt
  or or_1 (or_1_out, bl, cl, tl);
  or or_2 (or_2_out, br, cr, tr);
  and and_1 (and_1_out, lc, or_1_out);
  and and_2 (and_2_out, rc, or_2_out);
  and and_3 (and_3_out, lc, tl);
  or or_3 (out_8, and_1_out, and_2_out);
  or or_4 (top, and_3_out, and_4_out);
  and and_4 (and_4_out, rc, tr);
  or or_5 (center, and_6_out, and_5_out);
  and and_5 (and_5_out, rc, cr);
  and and_6 (and_6_out, lc, cl);
  or or_6 (bot, and_7_out, and_8_out);
  and and_7 (and_7_out, lc, bl);
  and and_8 (and_8_out, rc, br);
endmodule

module update_vy (
  input  top,
  input  center,
  input  bot,
  input  [2:0] old_vy,
  input  ds,
  output [2:0] \output 
);

  wire nor_1_out;
  wire [2:0] multiplexer_1_out, multiplexer_2_out;

  Multiplexer #(.width(3), .disabled(0), .enable("false")) multiplexer_1 (
    .in0(3'b001), .in1(3'b010), .out(multiplexer_1_out), .sel(ds));
  Multiplexer #(.width(3), .disabled(0), .enable("false")) multiplexer_2 (
    .in0(3'b111), .in1(3'b110), .out(multiplexer_2_out), .sel(ds));
  assign \output  = top ? multiplexer_1_out : 3'bz;  // Controlled_Buffer controlled_buffer_1
  assign \output  = center ? 3'b000 : 3'bz;  // Controlled_Buffer controlled_buffer_2
  assign \output  = bot ? multiplexer_2_out : 3'bz;  // Controlled_Buffer controlled_buffer_3
  nor nor_1 (nor_1_out, bot, center, top);
  assign \output  = nor_1_out ? old_vy : 3'bz;  // Controlled_Buffer controlled_buffer_4
endmodule
